# Fritzing sketch autorobot_complete (saved by Fritzing 0.8.0b)
breadboards: 1

parts:
  Part1 = Arduino Uno (Rev3)
  M1 = DC Motor
  M2 = DC Motor
  Part2 = Arduino Motor Shield (Rev3)
  U1 = mystery part, 7 pins [chip_label="Line scan sensor"]
  U2 = mystery part, 4 pins [chip_label="Distance sensor"]
  VCC1 = Battery
  VCC2 = Battery
  VCC3 = Battery
  VCC4 = Battery block 9V  # not connected

nets:
  N1: Part1.A0, U1.pin2
  N2: Part1.A1, U1.pin3
  N3: Part1.A2, U1.pin4
  N4: Part1.A3, U1.pin5
  N5: Part1.A4/SDA, U1.pin6
  N6: Part1.ICSP_MISO, Part1.D12/MISO, U2.pin2
  N7: Part1.ICSP_SCK, Part1.D13/SCK, U2.pin3
  GND: Part1.GND, Part2.GND, U1.pin7, U2.pin4, VCC1.-
  N8: Part1.D2, Part2.D12/DirA
  N9: Part1.D3_PWM, Part2.D11_PWM/B
  N10: Part1.D4, Part2.D13/DirB
  N11: Part1.D5_PWM, Part2.D3_PWM/A
  N12: Part1.5V, U1.pin1, U2.pin1
  N13: Part1.VIN, Part2.VMOT, VCC3.+
  N14: M1.pin_1, Part2.A+
  N15: M1.pin_2, Part2.A-
  N16: M2.pin_1, Part2.B+
  N17: M2.pin_2, Part2.B-
  N18: VCC1.+, VCC2.-
  N19: VCC2.+, VCC3.-

notes:
  GND
  SIDE
  5V
  Vin (max 12 V)
  ECHO - LOCATOR
  Vcc | Trig |Echo | GND
  5 POINT LINE SCANNER
  VCC | scanlines (S5 to S1) | GND
  Motor-Shield
  R-PWM: pin 5 to PW-A=A-1B
  L-PWM: pin 3 to PW-B = B-1B
  R-DIR : pin 4 to DIR-A= A-1A
  L-DIR : pin 2 to DIR-B = B-1A
  AA for more POWER !
  9V for the ARDUINO
  Motor A
  Motor B
